# Fritzing sketch Radar_Sketch (saved by Fritzing 0.9.3b)
breadboards: 1

parts:
  Part1 = Arduino Uno (Rev3)
  S1 = Pushbutton [package="[THT]"]
  J1 = Basic Servo
  LED1 = smd LED [color="Red (633nm)" package="0805 [SMD]"]
  LED2 = LED - 5mm [color="Red (633nm)" package="5 mm [THT]"]
  R1 = Resistor [tolerance=±5% resistance=220 package=THT]  # not connected
  R2 = Resistor [tolerance=±5% resistance=220 package=THT]
  HC-SR04_Sensor_1 = HC-SR04 Ultrasonic Distance Sensor

nets:
  N1: Part1.D8, HC-SR04_Sensor_1.TRIG
  N2: Part1.D3_PWM, S1.Pin_3, S1.Pin_4
  N3: Part1.D5_PWM, J1.pulse
  N4: Part1.D7, HC-SR04_Sensor_1.ECHO
  VCC: Part1.5V, J1.vcc, HC-SR04_Sensor_1.VCC
  GND: Part1.GND, S1.Pin_1, S1.Pin_2, J1.gnd, LED1.anode, LED2.anode, HC-SR04_Sensor_1.GND
  N5: LED2.cathode, R2.Pin_1
